# Fritzing sketch tukii (saved by Fritzing 1.0.4)
breadboards: 1

parts:
  Rotary_Encoder = Rotary Encoder [package=THT]
  part = Waveshare rp2040-zero tht [package=THT]
  128x64_0_96"_OLED = Grove OLED 128x96
  Left_Button = Square Pushbutton
  Right_Button = Square Pushbutton

nets:
  N1: Rotary_Encoder.EncoderPinA, part.Pin_21
  N2: Rotary_Encoder.EncoderPinC, Rotary_Encoder.SwitchrPinD, part.Pin_2, 128x64_0_96"_OLED.GND, Left_Button.leg0, Right_Button.leg0
  N3: Rotary_Encoder.EncoderPinB, part.Pin_20
  N4: Rotary_Encoder.SwitchPinE, part.Pin_9
  N5: part.Pin_3, 128x64_0_96"_OLED.VCC
  N6: part.Pin_5, Left_Button.leg1
  N7: part.Pin_7, Right_Button.leg1
  N8: part.Pin_18, 128x64_0_96"_OLED.SCL
  N9: part.Pin_19, 128x64_0_96"_OLED.SDA

custom parts:
  Rotary Encoder: Rotary Encoder from ALPSec11e with switch.
  Waveshare rp2040-zero tht: .RP2040-Zero, A Low-Cost, High-Performance Pico-Like MCU Board Based On Raspberry Pi Microcontroller RP2040. This varant is THT without the extra connections.
